# Fritzing sketch robot (saved by Fritzing 1.0.7)
# 18650 Li-ion Battery: CC-BY Dr Kristofer Chan, King's College London/Remote-research.org
breadboards: 2

parts:
  Mod2 = L298N DC motor driver
  M1 = DC Motor [voltage_(max)=6V voltage_(min)=3V]
  M2 = DC Motor [voltage_(max)=6V voltage_(min)=3V]
  Mod3 = L298N DC motor driver
  M3 = DC Motor [voltage_(max)=6V voltage_(min)=3V]
  M4 = DC Motor [voltage_(max)=6V voltage_(min)=3V]
  R1 = Resistor [tolerance=±5% power=0.25W resistance=15 package=THT]
  LED2 = LED - 5mm [color="Green (565nm)" current=0.030A package="5 mm [THT]"]
  LED3 = LED - 5mm [color="Red (633nm)" current=0.030A package="5 mm [THT]"]
  R2 = Resistor [tolerance=±5% power=0.25W resistance=150 package=THT]
  BAT1 = 18650 Li-ion Battery [package=battery-18650]
  BAT2 = 18650 Li-ion Battery [package=battery-18650]
  A1 = Raspberry Pi Pico2
  A2 = Raspberry Pi Pico2
  Mod4 = KY-023 Dual Axis Joystick Module [package="Breakout board"]

nets:
  N1: Mod2.OUT1, M1.pin_2
  N2: Mod2.OUT2, M1.pin_1
  12V: Mod2.12V, Mod2.5V-ENA-JMP-O, Mod3.12V, Mod3.5V-ENA-JMP-O, BAT1.+
  GND: Mod2.GND, Mod3.GND, LED2.cathode, LED3.cathode, BAT2.-, A2.pin_3, A2.pin_8, A2.pin_13, A2.pin_18, A2.pin_23, A2.pin_28, A2.pin_33, A2.pin_38
  N3: Mod2.OUT3, M2.pin_2
  N4: Mod2.OUT4, M2.pin_1
  N5: Mod2.ENA, A2.pin_11
  N6: Mod2.IN1, A2.pin_9
  N7: Mod2.IN2, A2.pin_7
  N8: Mod2.IN3, A2.pin_6
  N9: Mod2.IN4, A2.pin_5
  N10: Mod2.ENB, A2.pin_14
  N11: Mod3.OUT1, M3.pin_2
  N12: Mod3.OUT2, M3.pin_1
  N13: Mod3.5V, A2.pin_39
  N14: Mod3.OUT3, M4.pin_2
  N15: Mod3.OUT4, M4.pin_1
  N16: Mod3.ENA, A2.pin_31
  N17: Mod3.IN1, A2.pin_29
  N18: Mod3.IN2, A2.pin_27
  N19: Mod3.IN3, A2.pin_26
  N20: Mod3.IN4, A2.pin_25
  N21: Mod3.ENB, A2.pin_21
  N22: R1.Pin_0, A2.pin_20
  N23: R1.Pin_1, LED2.anode
  N24: LED3.anode, R2.Pin_1
  N25: R2.Pin_0, A2.pin_19
  N26: BAT1.-, BAT2.+
  N27: A1.pin_3, A1.pin_8, A1.pin_13, A1.pin_18, A1.pin_23, A1.pin_28, A1.pin_33, A1.pin_38, A1.pin_42, Mod4.GND
  N28: A1.pin_31, Mod4.VRx
  N29: A1.pin_32, Mod4.VRy
  N30: A1.pin_35, Mod4.+5V

custom parts:
  L298N DC motor driver: 2x DC motor driver with 78M05 positive voltage regulator (7..35 V) L298N: max 46 V, 2 A Set 5 V Enable jumper to enable 5 V regultor (needed for the L298N) and +5 V output at screw terminal or supply external +5 V at screw terminal Set ENA and/or ENB to +5 V to enable motor permanently or supply ENA and/or ENB with PWM signal IN1 and IN2 set rotation directory for motor A (OUT1/OUT2) IN2 and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
  18650 Li-ion Battery: 18650 li-ion Battery Standard 18650 battery with interactive connectors Creative Common Attribution 4.0 International (CC-BY 4.0) license. Any use of this part requires attribution of Dr Kristofer Chan, Department of Geography, King's College London. Contact kristofer.chan [at] kcl.ac.uk OR kris [at] remote-research.org for further information.
  Raspberry Pi Pico2: Raspberry Pi Pico 2W is our new $7 microcontroller board, built on RP2350: our new high-performance, secure microcontroller with on board WiFi.
  KY-023 Dual Axis Joystick Module: KY-023 Dual-Axis Joystick Module.
